# Fritzing sketch circuit (saved by Fritzing 0.9.3b)
breadboards: 1

parts:
  부품1 = Arduino Nano (Rev3.0)
  U1 = Sharp Dust Sensor [part_number=GP2Y1010AU0F]
  C3 = Electrolytic Capacitor [capacitance=1µF package="100 mil [THT, electrolytic]"]
  R1 = Resistor [tolerance=±5% resistance=220 package=THT]
  LCD1 = LCD screen
  LCM1602_IIC1 = LCM1602 IIC [part_number="LCM1602 IIC" chip_label="LCM1602 IIC" package="DIP (Dual Inline) [THT]"]
  VCC1 = 4 x AAA Battery Mount
  F1 = Fan - Ventilador [package=THT]
  F2 = Fan - Ventilador [package=THT]

nets:
  GND: 부품1.GND, U1.LED-GND, U1.S-GND, C3.-, LCM1602_IIC1.GND, VCC1.-, F1.GND, F2.GND
  N1: 부품1.D2, U1.LED
  5V: 부품1.VIN, VCC1.+, F1.5V, F2.5V
  VCC: 부품1.5V, U1.VCC, R1.Pin_1, LCM1602_IIC1.VCC
  N2: 부품1.A0, U1.Vo
  N3: U1.V-LED, C3.+, R1.Pin_0
  VSS: LCD1.VSS, LCM1602_IIC1.VSS
  VDD: LCD1.VDD, LCM1602_IIC1.VDD
  N4: LCD1.V0, LCM1602_IIC1.V0
  N5: LCD1.RS, LCM1602_IIC1.RS
  N6: LCD1.R/W, LCM1602_IIC1.RW
  N7: LCD1.E, LCM1602_IIC1.E
  N8: LCD1.DB0, LCM1602_IIC1.D0
  N9: LCD1.DB1, LCM1602_IIC1.D1
  N10: LCD1.DB2, LCM1602_IIC1.D2
  N11: LCD1.DB3, LCM1602_IIC1.D3
  N12: LCD1.DB4, LCM1602_IIC1.D4
  N13: LCD1.DB5, LCM1602_IIC1.D5
  N14: LCD1.DB6, LCM1602_IIC1.D6
  N15: LCD1.DB7, LCM1602_IIC1.D7
  N16: LCD1.LED+, LCM1602_IIC1.A
  N17: LCD1.LED-, LCM1602_IIC1.K

custom parts:
  Sharp Dust Sensor: Sharp GP2Y1010AU0F Dust Sensor
  LCM1602 IIC: I2C-Module to use a 1602 or 2004 LCD on with the wire.h libory Serial LCD Modul
  Fan - Ventilador: Ventilador de 2 pines, se encuentra comunmente en computadoras de escritorio
